# Fritzing sketch branchements (saved by Fritzing 0.9.3b)

parts:
  Adafruit_HUZZAH_ESP8266_Breakout1 = Adafruit HUZZAH ESP8266 Breakout [part_number=2471]
  BOX_1 = PIR sensor
  BOX_2 = PIR sensor
  BOX_3 = PIR sensor
  Power_plug1 = Power plug
  USBTTL1 = USB TTL Serial Cable
  BOX_4 = PIR sensor

nets:
  GND: Adafruit_HUZZAH_ESP8266_Breakout1.GND, Power_plug1.GND, USBTTL1.GND, BOX_4.GND
  N1: Adafruit_HUZZAH_ESP8266_Breakout1.VBat, Power_plug1.VCC
  N2: Adafruit_HUZZAH_ESP8266_Breakout1.V+#3, BOX_1.VDD
  N3: Adafruit_HUZZAH_ESP8266_Breakout1.#13, BOX_2.SIG
  N4: Adafruit_HUZZAH_ESP8266_Breakout1.#12, BOX_1.SIG
  N5: Adafruit_HUZZAH_ESP8266_Breakout1.#14, BOX_3.SIG
  N6: Adafruit_HUZZAH_ESP8266_Breakout1.#16, Adafruit_HUZZAH_ESP8266_Breakout1.RST
  N7: Adafruit_HUZZAH_ESP8266_Breakout1.TX, USBTTL1.RX
  N8: Adafruit_HUZZAH_ESP8266_Breakout1.RX, USBTTL1.TX
  N9: Adafruit_HUZZAH_ESP8266_Breakout1.#15, BOX_4.SIG
  N10: Adafruit_HUZZAH_ESP8266_Breakout1.V+#22, USBTTL1.5V
