# Fritzing sketch branchements (saved by Fritzing 0.9.3b)

parts:
  Adafruit_HUZZAH_ESP8266_Breakout1 = Adafruit HUZZAH ESP8266 Breakout [part_number=2471]
  PIR2 = PIR sensor
  PIR3 = PIR sensor
  PIR4 = PIR sensor
  Power_plug1 = Power plug
  USBTTL1 = USB TTL Serial Cable

nets:
  GND: Adafruit_HUZZAH_ESP8266_Breakout1.GND, PIR4.GND, Power_plug1.GND, USBTTL1.GND
  N1: Adafruit_HUZZAH_ESP8266_Breakout1.VBat, Power_plug1.VCC
  N2: Adafruit_HUZZAH_ESP8266_Breakout1.V+#3, PIR2.VDD
  N3: Adafruit_HUZZAH_ESP8266_Breakout1.#12, PIR2.SIG
  N4: Adafruit_HUZZAH_ESP8266_Breakout1.#14, PIR3.SIG
  N5: Adafruit_HUZZAH_ESP8266_Breakout1.#16, PIR4.SIG
  N6: Adafruit_HUZZAH_ESP8266_Breakout1.TX, USBTTL1.RX
  N7: Adafruit_HUZZAH_ESP8266_Breakout1.RX, USBTTL1.TX
  N8: Adafruit_HUZZAH_ESP8266_Breakout1.V+#22, USBTTL1.5V
